# Fritzing sketch DivaPlanCMasterShield (saved by Fritzing 0.7.10b)
breadboards: 1

parts:
  Arduino1 = Arduino
  microSD1 = MicroSD Breakout
  J1 = female pin header, 3 pins [form="♀ (female)"]
  J2 = female pin header, 3 pins [form="♀ (female)"]
  J3 = female pin header, 3 pins [form="♀ (female)"]
  J4 = female pin header, 3 pins [form="♀ (female)"]
  J5 = female pin header, 3 pins [form="♀ (female)"]

nets:
  N1: Arduino1.aref, microSD1.5V
  GND: Arduino1.GND, microSD1.GND, J1.pin1, J2.pin1, J3.pin1, J4.pin1, J5.pin1
  N2: Arduino1.D13, microSD1.CLK
  N3: Arduino1.D12, microSD1.DO
  N4: Arduino1.D11, microSD1.DI
  N5: Arduino1.D10, microSD1.CS
  N6: Arduino1.D9, microSD1.CD
  N7: Arduino1.A4, J1.pin2, J2.pin2, J3.pin2, J4.pin2, J5.pin2
  N8: Arduino1.A5, J1.pin3, J2.pin3, J3.pin3, J4.pin3, J5.pin3

notes:
  Diva Plan C Master

custom parts:
  MicroSD Breakout: 5V-ready microSD Breakout with Level Shifter
