# Fritzing sketch DivaPlanCSlaveShield (saved by Fritzing 0.7.10b)
breadboards: 1

parts:
  Diva_Slave_Plan_C = Arduino
  OLED1 = 128x32 SPI Monochrome OLEDDisplay
  OLED2 = 128x32 SPI Monochrome OLEDDisplay
  OLED3 = 128x32 SPI Monochrome OLEDDisplay
  Addr = female pin header, 3 pins [form="♀ (female)"]
  I2C_Bus = female pin header, 3 pins [form="♀ (female)"]
  5V = female pin header, 3 pins [form="♀ (female)"]
  GND = female pin header, 3 pins [form="♀ (female)"]
  Buttons1 = female pin header, 2 pins [form="♀ (female)"]
  Buttons2 = female pin header, 2 pins [form="♀ (female)"]
  R1 = Resistor [tolerance=±5% resistance=220 package=THT]
  R2 = Resistor [tolerance=±5% resistance=220 package=THT]
  R3 = Resistor [tolerance=±5% resistance=220 package=THT]
  R4 = Resistor [tolerance=±5% resistance=220 package=THT]
  Buttons3 = female pin header, 2 pins [form="♀ (female)"]
  R5 = Resistor [tolerance=±5% resistance=220 package=THT]
  R6 = Resistor [tolerance=±5% resistance=220 package=THT]

nets:
  GND: Diva_Slave_Plan_C.GND, OLED1.GND, OLED2.GND, OLED3.GND, I2C_Bus.pin1, GND.pin1, GND.pin2, GND.pin3
  N1: Diva_Slave_Plan_C.D13, OLED1.D/C, OLED2.D/C, OLED3.D/C
  N2: Diva_Slave_Plan_C.D12, OLED1.CLK, OLED2.CLK, OLED3.CLK
  N3: Diva_Slave_Plan_C.D11, OLED1.DATA, OLED2.DATA, OLED3.DATA
  N4: Diva_Slave_Plan_C.D10, OLED1.RST, OLED2.RST, OLED3.RST
  N5: Diva_Slave_Plan_C.D9, OLED3.CS
  N6: Diva_Slave_Plan_C.D8, OLED2.CS
  N7: Diva_Slave_Plan_C.D7, OLED1.CS
  N8: Diva_Slave_Plan_C.D4, Addr.pin1
  N9: Diva_Slave_Plan_C.D3, Addr.pin2
  N10: Diva_Slave_Plan_C.D2, Addr.pin3
  VIN: Diva_Slave_Plan_C.+5V, OLED1.VIN, OLED2.VIN, OLED3.VIN, 5V.pin1, 5V.pin2, 5V.pin3
  N11: Diva_Slave_Plan_C.A0, R1.Pin_1
  N12: Diva_Slave_Plan_C.A1, R3.Pin_1
  N13: Diva_Slave_Plan_C.A2, R5.Pin_1
  N14: Diva_Slave_Plan_C.A4, I2C_Bus.pin2
  N15: Diva_Slave_Plan_C.A5, I2C_Bus.pin3
  N16: Buttons1.pin1, R1.Pin_0, R2.Pin_1
  N17: Buttons1.pin2, R2.Pin_0
  N18: Buttons2.pin1, R3.Pin_0, R4.Pin_1
  N19: Buttons2.pin2, R4.Pin_0
  N20: Buttons3.pin1, R5.Pin_0, R6.Pin_1
  N21: Buttons3.pin2, R6.Pin_0

custom parts:
  128x32 SPI Monochrome OLEDDisplay: 128x32 SPI OLED Monochrome Display
